# Fritzing sketch arduino-01 (saved by Fritzing 0.5.2b)
breadboards: 1

parts:
  Arduino1 = Arduino
  LED1 = Red LED - 5mm [package="5 mm [THT]"]
  LED3 = Red LED - 5mm [package="5 mm [THT]"]
  LED5 = Red LED - 5mm [package="5 mm [THT]"]
  LED2 = yellow LED - 5mm [package="5 mm [THT]"]
  LED4 = green LED - 5mm [package="5 mm [THT]"]
  LED6 = yellow LED - 5mm [package="5 mm [THT]"]
  LED7 = Red LED - 5mm [package="5 mm [THT]"]
  U1 = mystery part, 2 pins [chip_label=Lautsprecher spacing=300mil]
  U2 = mystery part, 2 pins [chip_label=Lautsprecher spacing=300mil]

nets:
  N1: Arduino1.GND, LED1.cathode, LED3.cathode, LED5.cathode, LED2.cathode, LED4.cathode, LED6.cathode, LED7.cathode, U1.pin1, U2.pin1
  N2: Arduino1.D13, LED1.anode
  N3: Arduino1.D12, LED2.anode
  N4: Arduino1.D11, LED3.anode
  N5: Arduino1.D10, LED4.anode
  N6: Arduino1.D9, LED5.anode
  N7: Arduino1.D8, LED6.anode
  N8: Arduino1.D7, LED7.anode
  N9: Arduino1.D6, U1.pin2
  N10: Arduino1.D5, U2.pin2
