# Fritzing sketch arduino-02 (saved by Fritzing 0.5.2b)
breadboards: 1

parts:
  Arduino1 = Arduino
  LED1 = Red LED - 5mm [package="5 mm [THT]"]
  LED2 = Red LED - 5mm [package="5 mm [THT]"]
  S1 = Pushbutton [package=THT]
  J1 = Basic Servo

nets:
  GND: Arduino1.GND, LED1.cathode, LED2.cathode, S1.leg1, J1.gnd
  N1: Arduino1.D9, J1.pulse
  N2: Arduino1.D4, S1.leg0
  N3: Arduino1.D3, LED1.anode
  N4: Arduino1.D2, LED2.anode
  +5V: Arduino1.+5V, J1.vcc
